# Fritzing sketch Tag (saved by Fritzing 0.9.3b)
breadboards: 1

parts:
  Module1 = Decawave DWM1000 Adapter Board [package="Custom 27.7mm x 33.4mm"]
  Part1 = Arduino Uno (Rev3) - ICSP
  Part2 = Bluetooth HC-05 Macho  # not connected
  LED1 = LEDs [package=led10mm]
  R1 = Resistor [tolerance=±5% resistance=220 package="0603 [SMD]"]

nets:
  N1: Module1.RSTn, Part1.D9_PWM
  VDD: Module1.VDD, Part1.3V3
  N2: Module1.SPICSn, Part1.D10_PWM/SS
  N3: Module1.SPIMOSI, Part1.D11_PWM/MOSI
  N4: Module1.SPIMISO, Part1.ICSP_MISO, Part1.D12/MISO
  N5: Module1.SPICLK, Part1.D13/SCK
  N6: Module1.GPIO8_/_IRQ, Part1.D2
  GND: Module1.GND, Part1.GND
  N7: Part1.D3_PWM, LED1.A
  N8: LED1.C, R1.Pin_1

custom parts:
  Decawave DWM1000 Adapter Board: Adapter Board 0.1 in for the Decawave DWM1000 UWB RF module
